// Logisim project projetopentregar.circ as structural Verilog: 4 circuits, main circuit main
module main (
  input  RST
);

  wire CLK;

  Clock u_CLK (.out(CLK));
endmodule

module IntructionF (
  input  CLK,
  input  RST,
  output [15:0] Instrucao
);

  wire [7:0] adder_1_out, PC_q;

  Register PC (.D(adder_1_out), .en(1'b1), .clk(CLK), .Q(PC_q), .clr(RST));
  // Probe on adder_1_out
  // ROM #(.line("dual")) rom_1: pin names not known; wires that end beside it: PC_q
  Adder adder_1 (.a(8'h2), .b(PC_q), .out(adder_1_out));  // open: cin, cout
endmodule

module InstuctionD (
  input  [15:0] Intrucao,
  output [2:0] funct,
  output [2:0] rs2,
  output [2:0] rs1,
  output [2:0] rd,
  output [3:0] opcode,
  output [5:0] I_imm,
  output [5:0] S_offset,
  output [5:0] B_offset,
  output [8:0] J_offset
);


  assign B_offset = Intrucao[5:0];
  assign funct = Intrucao[2:0];
  assign I_imm = Intrucao[5:0];
  assign J_offset = Intrucao[8:0];
  assign opcode = Intrucao[15:12];
  assign rd = Intrucao[11:9];
  assign rs1 = Intrucao[8:6];
  assign rs2 = Intrucao[5:3];
  assign S_offset = Intrucao[5:0];

  // Other names for the same wires on the sheet: opcde[3:0] = Intrucao[15:12]

  // Notes on the sheet:
  //   Imetiato Tipo I
  //   Offset Tipo B
  //   Offset Tipo S
  //   Offset Tipo J
endmodule

module BR (
  input  CLK,
  input  RST,
  input  RegWrite,
  input  [2:0] RS1,
  input  [2:0] RS2,
  input  [2:0] RD,
  input  [15:0] Data
);

  Register #(.width(16)) R0 (.D({16{1'b0}}), .clk(CLK), .clr(RST));  // open: en, Q

  // Other names for the same wires on the sheet: RW = RegWrite
endmodule
